# Fritzing sketch diagram (saved by Fritzing 0.9.3b)
breadboards: 1

parts:
  パーツ1 = Arduino Uno (Rev3)
  VCC1 = Battery
  U1 = TA7291P [package=HSIP10-P-2.54(THT)]
  R1 = Resistor [tolerance=±5% resistance=220 package=THT]
  M1 = DC Motor
  U2 = TA7291P [package=HSIP10-P-2.54(THT)]
  R2 = Resistor [tolerance=±5% resistance=220 package=THT]
  M2 = DC Motor
  S1 = Pushbutton [package="[THT]"]
  R3 = Resistor [tolerance=±5% resistance=220 package=THT]

nets:
  N1: パーツ1.D9_PWM, U2.IN2
  N2: パーツ1.D10_PWM/SS, U2.IN1, R2.Pin_0
  N3: パーツ1.D5_PWM, U1.IN2
  N4: パーツ1.D6_PWM, U1.IN1
  N5: パーツ1.D7, R3.Pin_1
  VCC: パーツ1.5V, U1.Vcc, U2.Vcc, R2.Pin_1
  GND: パーツ1.GND, VCC1.-, U1.GND, U2.GND, S1.Pin_3, S1.Pin_4
  N6: VCC1.+, U1.Vs, R1.Pin_0, U2.Vs
  N7: U1.OUT1, M1.pin_1
  N8: U1.Vref, R1.Pin_1
  N9: U2.OUT1, M2.pin_1
  N10: U2.OUT2, M2.pin_2
  N11: S1.Pin_1, S1.Pin_2, R3.Pin_0

custom parts:
  TA7291P: The IC are Full-Bridge Driver. 4 modes available (CW / CCW / STOP / BRAKE) and PWM control. Output current:1.0 A (AVE.) 2.0 A (PEAK)
